// Logisim project SynthBite16.circ as structural Verilog: 1 circuit, main circuit SynthBite16
module SynthBite16 (
  input  in_1,
  input  [15:0] in_2,
  input  [15:0] in_3,
  input  in_4,
  input  in_5
);

  wire AC_p1, AC_p2, AC_p3, AC_p18, AC_p19, AC_p20, AC_p21, AC_p22, AC_p23, AC_p24, AC_p25, AC_p26, AC_p27,
       AC_p28, AC_p29, adder_1_cout, adder_3_cout, and_3_out, and_4_out, controlled_buffer_1_out,
       controlled_buffer_2_out, controlled_buffer_3_out, controlled_buffer_4_out, controlled_buffer_5_out,
       controlled_buffer_6_out, controlled_buffer_7_out, controlled_buffer_8_out, controlled_buffer_9_out,
       controlled_buffer_10_out, controlled_buffer_11_out, controlled_buffer_12_out,
       controlled_buffer_13_out, controlled_buffer_14_out, controlled_buffer_15_out,
       controlled_buffer_16_out, decoder_1_out0, decoder_1_out1, decoder_1_out2, decoder_1_out3,
       decoder_1_out10, decoder_2_out0, decoder_2_out1, decoder_2_out3, decoder_2_out10, decoder_2_out11,
       decoder_2_out12, decoder_2_out13, nand_1_out, not_2_out, or_2_out, or_3_out, or_4_out,
       subtractor_1_bout, undriven, undriven_2, undriven_7, undriven_8, undriven_9, undriven_10;
  wire [0:0] DR_q;
  wire [3:0] CWR_q;
  wire [9:0] CAR_q, undriven_5;
  wire [11:0] controlled_buffer_17_out, PC_q;
  wire [15:0] adder_1_out, adder_2_out, adder_3_out, and_1_out, and_2_out, DR_q_2, IR_q, mAC_p1, not_1_out,
       or_1_out, rand_q, register_2_q, register_3_q, subtractor_1_out, undriven_3, undriven_6, xor_1_out;
  wire [15:15] controlled_buffer_29_out, MasterClock_out, undriven_4;
  wire [23:0] CNTRL_MEM_data, CWR_q_2;

  Controlled_Buffer controlled_buffer_1 (.out(controlled_buffer_1_out), .en(undriven));  // open: in
  Controlled_Buffer controlled_buffer_2 (.out(controlled_buffer_2_out), .en(undriven));  // open: in
  Controlled_Buffer controlled_buffer_3 (.out(controlled_buffer_3_out), .en(undriven));  // open: in
  Controlled_Buffer controlled_buffer_4 (.out(controlled_buffer_4_out), .en(undriven));  // open: in
  Controlled_Buffer controlled_buffer_5 (.out(controlled_buffer_5_out), .en(undriven));  // open: in
  Controlled_Buffer controlled_buffer_6 (.out(controlled_buffer_6_out), .en(undriven));  // open: in
  Controlled_Buffer controlled_buffer_7 (.out(controlled_buffer_7_out), .en(undriven));  // open: in
  Controlled_Buffer controlled_buffer_8 (.out(controlled_buffer_8_out), .en(undriven));  // open: in
  Controlled_Buffer controlled_buffer_9 (.out(controlled_buffer_9_out), .en(undriven));  // open: in
  Controlled_Buffer controlled_buffer_10 (.out(controlled_buffer_10_out), .en(undriven));  // open: in
  Controlled_Buffer controlled_buffer_11 (.out(controlled_buffer_11_out), .en(undriven));  // open: in
  Controlled_Buffer controlled_buffer_12 (.out(controlled_buffer_12_out), .en(undriven));  // open: in
  Controlled_Buffer controlled_buffer_13 (.out(controlled_buffer_13_out), .en(undriven));  // open: in
  Controlled_Buffer controlled_buffer_14 (.out(controlled_buffer_14_out), .en(undriven));  // open: in
  Controlled_Buffer controlled_buffer_15 (.out(controlled_buffer_15_out), .en(undriven));  // open: in
  Controlled_Buffer controlled_buffer_16 (.out(controlled_buffer_16_out), .en(undriven));  // open: in
  Clock MasterClock (.out(MasterClock_out[15]));
  LED led_1 (.in(MasterClock_out[15]));
  Register #(.width(16)) DR (
    .D({{4{controlled_buffer_29_out[15]}}, controlled_buffer_17_out}), .en(decoder_2_out10),
    .clk(MasterClock_out[15]), .Q({DR_q_2[14:0], DR_q[0]}), .clr(undriven_2));
  LedBar #(.matrixcols(4)) ledbar_1 (
    .led0(controlled_buffer_29_out[15]), .led1(controlled_buffer_29_out[15]),
    .led2(controlled_buffer_29_out[15]), .led3(controlled_buffer_29_out[15]));
  DotMatrix #(.matrixcols(16), .matrixrows(1)) dotmatrix_1 (
    .col0(controlled_buffer_29_out[15]), .col1(controlled_buffer_29_out[15]),
    .col2(controlled_buffer_29_out[15]), .col3(controlled_buffer_29_out[15]),
    .col4(controlled_buffer_17_out[11]), .col5(controlled_buffer_17_out[10]),
    .col6(controlled_buffer_17_out[9]), .col7(controlled_buffer_17_out[8]),
    .col8(controlled_buffer_17_out[7]), .col9(controlled_buffer_17_out[6]),
    .col10(controlled_buffer_17_out[5]), .col11(controlled_buffer_17_out[4]),
    .col12(controlled_buffer_17_out[3]), .col13(controlled_buffer_17_out[2]),
    .col14(controlled_buffer_17_out[1]), .col15(controlled_buffer_17_out[0]));
  assign controlled_buffer_17_out[0] = decoder_1_out3 ? PC_q[0] : 1'bz;  // Controlled_Buffer controlled_buffer_17
  assign controlled_buffer_17_out[1] = decoder_1_out3 ? PC_q[1] : 1'bz;  // Controlled_Buffer controlled_buffer_18
  assign controlled_buffer_17_out[2] = decoder_1_out3 ? PC_q[2] : 1'bz;  // Controlled_Buffer controlled_buffer_19
  assign controlled_buffer_17_out[3] = decoder_1_out3 ? PC_q[3] : 1'bz;  // Controlled_Buffer controlled_buffer_20
  assign controlled_buffer_17_out[4] = decoder_1_out3 ? PC_q[4] : 1'bz;  // Controlled_Buffer controlled_buffer_21
  assign controlled_buffer_17_out[5] = decoder_1_out3 ? PC_q[5] : 1'bz;  // Controlled_Buffer controlled_buffer_22
  assign controlled_buffer_17_out[6] = decoder_1_out3 ? PC_q[6] : 1'bz;  // Controlled_Buffer controlled_buffer_23
  assign controlled_buffer_17_out[7] = decoder_1_out3 ? PC_q[7] : 1'bz;  // Controlled_Buffer controlled_buffer_24
  assign controlled_buffer_17_out[8] = decoder_1_out3 ? PC_q[8] : 1'bz;  // Controlled_Buffer controlled_buffer_25
  assign controlled_buffer_17_out[9] = decoder_1_out3 ? PC_q[9] : 1'bz;  // Controlled_Buffer controlled_buffer_26
  assign controlled_buffer_17_out[10] = decoder_1_out3 ? PC_q[10] : 1'bz;  // Controlled_Buffer controlled_buffer_27
  assign controlled_buffer_17_out[11] = decoder_1_out3 ? PC_q[11] : 1'bz;  // Controlled_Buffer controlled_buffer_28
  assign controlled_buffer_29_out[15] = decoder_1_out3 ? in_5 : 1'bz;  // Controlled_Buffer controlled_buffer_29
  Register #(.width(12)) PC (
    .D(controlled_buffer_17_out), .en(decoder_2_out3), .clk(MasterClock_out[15]), .Q(PC_q));  // open: clr
  Register #(.width(16)) IR (
    .D({{4{controlled_buffer_29_out[15]}}, controlled_buffer_17_out}), .en(decoder_2_out11),
    .clk(MasterClock_out[15]), .Q(IR_q));  // open: clr
  Register register_1 (.en(in_1), .clk(MasterClock_out[15]));  // open: D, Q, clr
  Adder #(.width(16)) adder_1 (
    .a({DR_q_2[14:0], DR_q[0]}), .b({{4{controlled_buffer_29_out[15]}}, controlled_buffer_17_out}),
    .out(adder_1_out), .cin(DR_q_2[15]), .cout(adder_1_cout));
  Subtractor #(.width(16)) subtractor_1 (
    .a({DR_q_2[14:0], DR_q[0]}), .b({{4{controlled_buffer_29_out[15]}}, controlled_buffer_17_out}),
    .out(subtractor_1_out), .bin(DR_q_2[15]), .bout(subtractor_1_bout));
  assign or_1_out = {{4{controlled_buffer_29_out[15]}}, controlled_buffer_17_out} | {DR_q_2[14:0], DR_q[0]};  // OR_Gate or_1, 16 bits wide
  Counter #(.max('h3f), .width(6)) tim (.clk(MasterClock_out[15]));  // open: clr, load, up, count, D, carry, Q
  or or_2 (or_2_out, adder_1_cout, subtractor_1_bout);
  assign xor_1_out = {{4{controlled_buffer_29_out[15]}}, controlled_buffer_17_out} ^ {DR_q_2[14:0], DR_q[0]};  // XOR_Gate xor_1, 16 bits wide
  or or_3 (or_3_out, or_2_out, or_4_out);
  or or_4 (or_4_out, DR_q[0], adder_3_cout);
  assign and_1_out = {{4{controlled_buffer_29_out[15]}}, controlled_buffer_17_out} & {DR_q_2[14:0], DR_q[0]};  // AND_Gate and_1, 16 bits wide
  Register #(.width(16)) \rand  (.D(undriven_3), .clk(MasterClock_out[15]), .Q(rand_q));  // open: en, clr
  Register #(.width(16)) register_2 (
    .D({{4{controlled_buffer_29_out[15]}}, controlled_buffer_17_out}), .en(decoder_2_out12),
    .clk(MasterClock_out[15]), .Q(register_2_q));  // open: clr
  Adder #(.width(16)) adder_2 (
    .a(in_3), .b({{4{controlled_buffer_29_out[15]}}, controlled_buffer_17_out}), .out(adder_2_out));  // open: cin, cout
  assign and_2_out = {DR_q_2[14:0], DR_q[0]} & {16{undriven_4[15]}};  // AND_Gate and_2, 16 bits wide
  Comparator #(.width(16)) comparator_1 (
    .a({{4{controlled_buffer_29_out[15]}}, controlled_buffer_17_out}), .b({DR_q_2[14:0], DR_q[0]}));  // open: gt, eq, lt
  Hex_Digit_Display #(.decimalPoint("false")) hex_digit_display_1 (.value(register_2_q[15:12]));
  Hex_Digit_Display #(.decimalPoint("false")) hex_digit_display_2 (.value(register_2_q[11:8]));
  // Shift_Register #(.length(16)) mAC: pin names not known; wires that end beside it: mAC_p1, CWR_q_2[14], CWR_q_2[15], MasterClock_out[15], in_4, mAC_p1[0], mAC_p1[1], mAC_p1[2], mAC_p1[3], mAC_p1[4], mAC_p1[5], mAC_p1[6], mAC_p1[7], mAC_p1[8], mAC_p1[9], mAC_p1[10], mAC_p1[11]
  Adder #(.width(16)) adder_3 (.a(mAC_p1), .b(and_2_out), .out(adder_3_out), .cin(in_4), .cout(adder_3_cout));
  Hex_Digit_Display #(.decimalPoint("false")) hex_digit_display_3 (.value(register_2_q[7:4]));
  Hex_Digit_Display #(.decimalPoint("false")) hex_digit_display_4 (.value(register_2_q[3:0]));
  Register #(.width(10)) CAR (.D(undriven_5), .en(1'b1), .clk(MasterClock_out[15]), .Q(CAR_q));  // open: clr
  assign not_1_out = ~{DR_q_2[14:0], DR_q[0]};  // NOT_Gate not_1, 16 bits wide
  ROM #(.addrWidth(10), .dataWidth(24)) CNTRL_MEM (.addr(CAR_q), .data(CNTRL_MEM_data));
  Register #(.trigger("falling"), .width(24)) CWR (
    .D(CNTRL_MEM_data), .en(1'b1), .clk(MasterClock_out[15]), .Q({CWR_q_2[23:12], CWR_q, CWR_q_2[7:0]}));  // open: clr
  Multiplexer #(.enable("true"), .select(4), .width(16)) multiplexer_1 (
    .in0({DR_q_2[14:0], DR_q[0]}), .in1(not_1_out), .in2(adder_1_out), .in3(subtractor_1_out),
    .in4(or_1_out), .in5(xor_1_out), .in6(and_1_out), .in7(DR_q_2), .in8(in_2), .in9(rand_q),
    .in10(adder_2_out), .in11(mAC_p1), .in12(undriven_6), .in13(in_2), .in14(in_2), .in15(in_2),
    .out({16{MasterClock_out[15]}}), .sel(CWR_q), .en(CWR_q_2[12]));
  DotMatrix #(.matrixcols(24), .matrixrows(1)) dotmatrix_2 (
    .col0(CWR_q_2[0]), .col1(CWR_q_2[1]), .col2(CWR_q_2[2]), .col3(CWR_q_2[3]), .col4(CWR_q_2[4]),
    .col5(CWR_q_2[5]), .col6(CWR_q_2[6]), .col7(CWR_q_2[7]), .col8(CWR_q[0]), .col9(CWR_q[1]),
    .col10(CWR_q[2]), .col11(CWR_q[3]), .col12(CWR_q_2[12]), .col13(CWR_q_2[13]), .col14(CWR_q_2[14]),
    .col15(CWR_q_2[15]), .col16(CWR_q_2[16]), .col17(CWR_q_2[17]), .col18(CWR_q_2[18]), .col19(CWR_q_2[19]),
    .col20(CWR_q_2[20]), .col21(CWR_q_2[21]), .col22(CWR_q_2[22]), .col23(CWR_q_2[23]));
  nand nand_1 (nand_1_out, CWR_q[1], CWR_q[0]);
  not not_2 (not_2_out, CWR_q[2]);
  and and_3 (and_3_out, not_2_out, nand_1_out);
  and and_4 (and_4_out, CWR_q[3], and_3_out);
  // Shift_Register #(.length(16)) AC: pin names not known; wires that end beside it: AC_p1, AC_p2, AC_p3, MasterClock_out[15], DR_q_2[15], MasterClock_out[15], MasterClock_out[15], MasterClock_out[15], MasterClock_out[15], MasterClock_out[15], MasterClock_out[15], MasterClock_out[15], MasterClock_out[15], MasterClock_out[15], MasterClock_out[15], MasterClock_out[15], MasterClock_out[15], AC_p18, AC_p19, AC_p20, AC_p21, AC_p22, AC_p23, AC_p24, AC_p25, AC_p26, AC_p27, AC_p28, AC_p29
  RAM #(.addrWidth(12), .asyncread("true"), .dataWidth(16), .databus("bidir")) MEM (
    .addr(PC_q), .we(decoder_2_out1), .oe(decoder_1_out1), .clk(MasterClock_out[15]),
    .data({{4{controlled_buffer_29_out[15]}}, controlled_buffer_17_out}));
  Decoder #(.enable("false"), .select(4)) decoder_1 (
    .out0(decoder_1_out0), .out1(decoder_1_out1), .out2(decoder_1_out2), .out3(decoder_1_out3),
    .out10(decoder_1_out10), .sel(CWR_q_2[3:0]));  // open: out4, out5, out6, out7, out8, out9, out11, out12, out13, out14, out15
  Decoder #(.enable("false"), .select(4)) decoder_2 (
    .out0(decoder_2_out0), .out1(decoder_2_out1), .out2(AC_p2), .out3(decoder_2_out3),
    .out10(decoder_2_out10), .out11(decoder_2_out11), .out12(decoder_2_out12), .out13(decoder_2_out13),
    .sel(CWR_q_2[7:4]));  // open: out4, out5, out6, out7, out8, out9, out14, out15
  D_Flip_Flop carry (.D(or_3_out), .clk(MasterClock_out[15]));  // open: Q, Qn, preset, reset
  assign controlled_buffer_17_out[0] = decoder_1_out2 ? AC_p18 : 1'bz;  // Controlled_Buffer controlled_buffer_30
  assign controlled_buffer_17_out[1] = decoder_1_out2 ? AC_p19 : 1'bz;  // Controlled_Buffer controlled_buffer_31
  assign controlled_buffer_17_out[2] = decoder_1_out2 ? AC_p20 : 1'bz;  // Controlled_Buffer controlled_buffer_32
  assign controlled_buffer_17_out[3] = decoder_1_out2 ? AC_p21 : 1'bz;  // Controlled_Buffer controlled_buffer_33
  assign controlled_buffer_17_out[4] = decoder_1_out2 ? AC_p22 : 1'bz;  // Controlled_Buffer controlled_buffer_34
  assign controlled_buffer_17_out[5] = decoder_1_out2 ? AC_p23 : 1'bz;  // Controlled_Buffer controlled_buffer_35
  assign controlled_buffer_17_out[6] = decoder_1_out2 ? AC_p24 : 1'bz;  // Controlled_Buffer controlled_buffer_36
  assign controlled_buffer_17_out[7] = decoder_1_out2 ? AC_p25 : 1'bz;  // Controlled_Buffer controlled_buffer_37
  assign controlled_buffer_17_out[8] = decoder_1_out2 ? AC_p26 : 1'bz;  // Controlled_Buffer controlled_buffer_38
  assign controlled_buffer_17_out[9] = decoder_1_out2 ? AC_p27 : 1'bz;  // Controlled_Buffer controlled_buffer_39
  assign controlled_buffer_17_out[10] = decoder_1_out2 ? AC_p28 : 1'bz;  // Controlled_Buffer controlled_buffer_40
  assign controlled_buffer_17_out[11] = decoder_1_out2 ? AC_p29 : 1'bz;  // Controlled_Buffer controlled_buffer_41
  assign controlled_buffer_29_out[15] = decoder_1_out2 ? undriven_7 : 1'bz;  // Controlled_Buffer controlled_buffer_42
  assign controlled_buffer_29_out[15] = decoder_1_out2 ? undriven_8 : 1'bz;  // Controlled_Buffer controlled_buffer_43
  assign controlled_buffer_29_out[15] = decoder_1_out2 ? undriven_9 : 1'bz;  // Controlled_Buffer controlled_buffer_44
  assign controlled_buffer_29_out[15] = decoder_1_out2 ? undriven_4[15] : 1'bz;  // Controlled_Buffer controlled_buffer_45
  LED led_2 (.in(decoder_1_out0));
  LED led_3 (.in(decoder_2_out0));
  D_Flip_Flop d_ff_1 (.D(decoder_2_out13), .clk(MasterClock_out[15]), .Q(DR_q_2[15]));  // open: Qn, preset, reset
  or or_5 (AC_p3, and_4_out, CWR_q_2[13]);
  Counter #(.max('h7), .width(3)) SR ();  // open: clr, load, up, count, clk, D, carry, Q
  Register #(.width(16)) register_3 (.Q(register_3_q));  // open: D, en, clk, clr
  Register #(.width(16)) register_4 ();  // open: D, en, clk, Q, clr
  Register #(.width(16)) register_5 ();  // open: D, en, clk, Q, clr
  Register #(.width(16)) register_6 (.clr(undriven_10));  // open: D, en, clk, Q
  Register #(.width(16)) register_7 ();  // open: D, en, clk, Q, clr
  Register #(.width(16)) register_8 ();  // open: D, en, clk, Q, clr
  Register #(.width(16)) register_9 ();  // open: D, en, clk, Q, clr
  Register #(.width(16)) register_10 ();  // open: D, en, clk, Q, clr

  // Notes on the sheet:
  //   CLOCK
  //   SYSTEM BUS
  //   16 LINES
  //   PRESENT BUS VALUES
  //   ALU
  //   LEAST SIGNIFICANT LINE
  //   MOST SIGNIFICANT LINE
  //   OUTPUT
  //   CONTROL UNIT
  //   this line is just a place holder
  //   PRESENT CONTROL
  //   AC RESET ASYNC
  //   ACC SHIFT(L)
  //   NONE
  //   MEM OUT ENABLE
  //   ACC ON BUS
  //   PC ON BUS
  //   NONE
  //   AC PARLLEL LOAD
  //   PC LOAD
  //   DR LOAD
  //   IR LOAD
  //   OUT LOAD
  //   SRL IN
  //   PUT ON BUS
  //   MEM WRITE ENABLE
  //   SERIAL IN
  //   LOAD FROM BUS
endmodule
